# Fritzing sketch bttf_keypad (saved by Fritzing 0.9.3b)
perfboards: 1

parts:
  SA = Pushbutton [package="[THT]"]
  SB = Pushbutton [package="[THT]"]
  SC = Pushbutton [package="[THT]"]
  SD = Pushbutton [package="[THT]"]
  SE = Pushbutton [package="[THT]"]
  S4 = Pushbutton [package="[THT]"]
  S1 = Pushbutton [package="[THT]"]
  S7 = Pushbutton [package="[THT]"]
  S0 = Pushbutton [package="[THT]"]
  S5 = Pushbutton [package="[THT]"]
  S2 = Pushbutton [package="[THT]"]
  S8 = Pushbutton [package="[THT]"]
  S6 = Pushbutton [package="[THT]"]
  S3 = Pushbutton [package="[THT]"]
  S9 = Pushbutton [package="[THT]"]
  LED1 = LED - 5mm [color="Red (633nm)" package="5 mm [THT]"]
  LED2 = LED - 5mm [color="Yellow (585nm)" package="5 mm [THT]"]
  LED3 = LED - 5mm [color="Green (565nm)" package="5 mm [THT]"]
  LED4 = LED - 5mm [color="White (6500K)" package="5 mm [THT]"]
  LED5 = LED - 5mm [color="White (6500K)" package="5 mm [THT]"]
  J2 = male pin header, 5 pins [form="♂ (male)"]
  J1 = male pin header, 3 pins [form="♂ (male)"]
  D3 = Rectifier Diode [part_number=1N4148 package="300 mil [THT]"]
  D2 = Rectifier Diode [part_number=1N4148 package="300 mil [THT]"]
  D1 = Rectifier Diode [part_number=1N4148 package="300 mil [THT]"]
  J3 = male pin header, 6 pins [form="♂ (male)"]

nets:
  N1: SA.Pin_1, SA.Pin_2, SB.Pin_1, SB.Pin_2, SC.Pin_1, SC.Pin_2, J2.pin5
  N2: SA.Pin_3, SA.Pin_4, SD.Pin_3, SD.Pin_4, S4.Pin_3, S4.Pin_4, S1.Pin_3, S1.Pin_4, S7.Pin_3, S7.Pin_4, D1.cathode
  N3: SB.Pin_3, SB.Pin_4, S0.Pin_3, S0.Pin_4, S5.Pin_3, S5.Pin_4, S2.Pin_3, S2.Pin_4, S8.Pin_3, S8.Pin_4, D2.cathode
  N4: SC.Pin_3, SC.Pin_4, SE.Pin_3, SE.Pin_4, S6.Pin_3, S6.Pin_4, S3.Pin_3, S3.Pin_4, S9.Pin_3, S9.Pin_4, D3.cathode
  N5: SD.Pin_1, SD.Pin_2, SE.Pin_1, SE.Pin_2, S0.Pin_1, S0.Pin_2, J2.pin4
  N6: S4.Pin_1, S4.Pin_2, S5.Pin_1, S5.Pin_2, S6.Pin_1, S6.Pin_2, J2.pin2
  N7: S1.Pin_1, S1.Pin_2, S2.Pin_1, S2.Pin_2, S3.Pin_1, S3.Pin_2, J2.pin1
  N8: S7.Pin_1, S7.Pin_2, S8.Pin_1, S8.Pin_2, S9.Pin_1, S9.Pin_2, J2.pin3
  N9: LED1.cathode, J3.pin1
  N10: LED1.anode, LED2.anode, LED3.anode, LED4.anode, LED5.anode, J3.pin3
  N11: LED2.cathode, J3.pin2
  N12: LED3.cathode, J3.pin4
  N13: LED4.cathode, J3.pin5
  N14: LED5.cathode, J3.pin6
  N15: J1.pin1, D1.anode
  N16: J1.pin2, D2.anode
  N17: J1.pin3, D3.anode
