# Fritzing sketch mm5250_multiplex (saved by Fritzing 0.9.3b)
breadboards: 3

parts:
  IC1 = IC, DIP package, 40 pins [chip_label=MM5250]
  C1 = Ceramic Capacitor [capacitance=1nF package="100 mil [THT, multilayer]"]
  R1 = Trimmer Potentiometer [maximum_resistance=0.1MΩ package=THT]
  Q1 = PNP-Transistor [package="TO92 [THT]"]
  R2 = Resistor [tolerance=±5% resistance=1k package=THT]
  R3 = Resistor [tolerance=±5% resistance=10k package=THT]
  LED1 = LED - 3mm [color="Red (633nm)" package="3 mm [THT]"]
  R4 = Resistor [tolerance=±5% resistance=1k package=THT]
  Q2 = PNP-Transistor [package="TO92 [THT]"]
  R5 = Resistor [tolerance=±5% resistance=10k package=THT]
  LED2 = LED - 3mm [color="Yellow (592nm)" package="3 mm [THT]"]
  Q3 = PNP-Transistor [package="TO92 [THT]"]
  R6 = Resistor [tolerance=±5% resistance=10k package=THT]
  R7 = Resistor [tolerance=±5% resistance=1k package=THT]
  LED3 = LED - 3mm [color="Green (565nm)" package="3 mm [THT]"]
  Part1 = Arduino Uno (Rev3)

nets:
  N1: IC1.pin1, C1.0, Part1.GND
  N2: IC1.pin19, C1.1, R1.wiper
  N3: IC1.pin20, R1.leg2, Q1.E, R3.Pin_0, Q2.E, R5.Pin_0, Q3.E, R6.Pin_0, Part1.5V
  N4: IC1.pin21, Part1.D13/SCK
  N5: IC1.pin22, Part1.D11_PWM/MOSI
  N6: IC1.pin23, Part1.D8
  N7: IC1.pin24, R2.Pin_0
  N8: IC1.pin25, R4.Pin_0
  N9: IC1.pin26, R7.Pin_0
  N10: IC1.pin27, LED1.cathode, LED2.cathode, LED3.cathode
  N11: Q1.B, R2.Pin_1, R3.Pin_1
  N12: Q1.C, LED1.anode
  N13: R4.Pin_1, Q2.B, R5.Pin_1
  N14: Q2.C, LED2.anode
  N15: Q3.B, R6.Pin_1, R7.Pin_1
  N16: Q3.C, LED3.anode
