# Fritzing sketch timecircuit_display_row (saved by Fritzing 0.9.3b)
breadboards: 5
stripboards: 1
perfboards: 1

parts:
  IC1 = IC, DIP package, 40 pins [chip_label=MM5450]
  C1 = Ceramic Capacitor [capacitance=1nF package="100 mil [THT, multilayer]"]
  R1 = Trimmer Potentiometer [maximum_resistance=0.1MΩ package=THT]
  Q1 = PNP-Transistor [package="TO92 [THT]"]
  R2 = Resistor [tolerance=±5% resistance=1k package=THT]
  R3 = Resistor [tolerance=±5% resistance=10k package=THT]
  LED1 = LED - 3mm [color="Red (633nm)" package="3 mm [THT]"]
  R4 = Resistor [tolerance=±5% resistance=1k package=THT]
  Q2 = PNP-Transistor [package="TO92 [THT]"]
  R5 = Resistor [tolerance=±5% resistance=10k package=THT]
  LED2 = LED - 3mm [color="Yellow (592nm)" package="3 mm [THT]"]
  Q3 = PNP-Transistor [package="TO92 [THT]"]
  R6 = Resistor [tolerance=±5% resistance=10k package=THT]
  R7 = Resistor [tolerance=±5% resistance=1k package=THT]
  LED3 = LED - 3mm [color="Green (565nm)" package="3 mm [THT]"]
  Part1 = Arduino Uno (Rev3)
  7_Segment1 = 7 Segment Display
  7_Segment2 = 7 Segment Display
  7_Segment3 = 7 Segment Display
  7_Segment4 = 7 Segment Display
  7_Segment5 = 7 Segment Display
  7_Segment6 = 7 Segment Display
  7_Segment7 = 7 Segment Display
  7_Segment8 = 7 Segment Display
  7_Segment9 = 7 Segment Display
  7_Segment10 = 7 Segment Display
  LED4 = LED - 3mm [color="Yellow (585nm)" package="3 mm [THT]"]
  LED5 = LED - 3mm [color="Yellow (585nm)" package="3 mm [THT]"]
  LED6 = LED - 3mm [color="Yellow (585nm)" package="3 mm [THT]"]
  LED7 = LED - 3mm [color="Yellow (585nm)" package="3 mm [THT]"]
  14_Segment1 = 14segment_red [part_number=KWA-541CVB]
  14_Segment2 = 14segment_red [part_number=KWA-541CVB]
  Part2 = adafruit [part_number=1427]
  C2 = Electrolytic Capacitor [capacitance=0.22mF voltage=16V package="100 mil [THT, electrolytic]"]
  J3 = male pin header, 6 pins [form="♂ (male)"]
  J1 = male pin header, 3 pins [form="♂ (male)"]
  J2 = male pin header, 5 pins [form="♂ (male)"]

nets:
  N1: IC1.pin1, C1.0, Part1.GND, Part2.connector29, C2.-
  N2: IC1.pin2, 7_Segment1.Segment_B, 7_Segment5.Segment_B, 7_Segment9.Segment_B
  N3: IC1.pin3, 7_Segment1.Segment_A, 7_Segment5.Segment_A, 7_Segment9.Segment_A
  N4: IC1.pin4, 7_Segment1.Segment_F, 7_Segment5.Segment_F, 7_Segment9.Segment_F
  N5: IC1.pin5, 7_Segment1.Segment_G, 7_Segment5.Segment_G, 7_Segment9.Segment_G
  N6: IC1.pin6, 7_Segment2.Segment_B, 7_Segment6.Segment_B, 7_Segment10.Segment_B
  N7: IC1.pin7, 7_Segment2.Segment_A, 7_Segment6.Segment_A, 7_Segment10.Segment_A
  N8: IC1.pin8, 7_Segment2.Segment_F, 7_Segment6.Segment_F, 7_Segment10.Segment_F
  N9: IC1.pin9, 7_Segment2.Segment_G, 7_Segment6.Segment_G, 7_Segment10.Segment_G
  N10: IC1.pin10, 7_Segment3.Segment_B, 7_Segment7.Segment_B
  N11: IC1.pin11, 7_Segment3.Segment_A, 7_Segment7.Segment_A
  N12: IC1.pin12, 7_Segment3.Segment_F, 7_Segment7.Segment_F
  N13: IC1.pin13, 7_Segment3.Segment_G, 7_Segment7.Segment_G
  N14: IC1.pin14, 7_Segment4.Segment_B, 7_Segment8.Segment_B
  N15: IC1.pin15, 7_Segment4.Segment_A, 7_Segment8.Segment_A
  N16: IC1.pin16, 7_Segment4.Segment_F, 7_Segment8.Segment_F
  N17: IC1.pin17, 7_Segment4.Segment_G, 7_Segment8.Segment_G
  N18: IC1.pin18, LED5.cathode, LED7.cathode
  N19: IC1.pin19, C1.1, R1.wiper
  N20: IC1.pin20, R1.leg2, Q1.E, R3.Pin_0, Q2.E, R5.Pin_0, Q3.E, R6.Pin_0, Part1.5V, Part2.connector28, C2.+
  N21: IC1.pin21, Part1.D13/SCK
  N22: IC1.pin22, Part1.D11_PWM/MOSI
  N23: IC1.pin23, Part1.D9_PWM
  N24: IC1.pin24, R2.Pin_0
  N25: IC1.pin25, R4.Pin_0
  N26: IC1.pin26, R7.Pin_0
  N27: IC1.pin27, LED1.cathode, LED2.cathode, LED3.cathode
  N28: IC1.pin28, LED4.cathode, LED6.cathode
  N29: IC1.pin29, 7_Segment4.Segment_E, 7_Segment8.Segment_E, J3.pin6
  N30: IC1.pin30, 7_Segment4.Segment_D, 7_Segment8.Segment_D, J3.pin5
  N31: IC1.pin31, 7_Segment4.Segment_C, 7_Segment8.Segment_C, J3.pin4
  N32: IC1.pin32, 7_Segment3.Segment_E, 7_Segment7.Segment_E, J3.pin2
  N33: IC1.pin33, 7_Segment3.Segment_D, 7_Segment7.Segment_D, J3.pin1
  N34: IC1.pin34, 7_Segment3.Segment_C, 7_Segment7.Segment_C
  N35: IC1.pin35, 7_Segment2.Segment_E, 7_Segment6.Segment_E, 7_Segment10.Segment_E
  N36: IC1.pin36, 7_Segment2.Segment_D, 7_Segment6.Segment_D, 7_Segment10.Segment_D
  N37: IC1.pin37, 7_Segment2.Segment_C, 7_Segment6.Segment_C, 7_Segment10.Segment_C
  N38: IC1.pin38, 7_Segment1.Segment_E, 7_Segment5.Segment_E, 7_Segment9.Segment_E
  N39: IC1.pin39, 7_Segment1.Segment_D, 7_Segment5.Segment_D, 7_Segment9.Segment_D
  N40: IC1.pin40, 7_Segment1.Segment_C, 7_Segment5.Segment_C, 7_Segment9.Segment_C
  N41: Q1.B, R2.Pin_1, R3.Pin_1
  N42: Q1.C, LED1.anode, 7_Segment1.common_anode, 7_Segment2.common_anode, 7_Segment3.common_anode, 7_Segment4.common_anode, LED6.anode, LED7.anode
  N43: R4.Pin_1, Q2.B, R5.Pin_1
  N44: Q2.C, LED2.anode, 7_Segment5.common_anode, 7_Segment6.common_anode, 7_Segment7.common_anode, 7_Segment8.common_anode
  N45: Q3.B, R6.Pin_1, R7.Pin_1
  N46: Q3.C, LED3.anode, 7_Segment9.common_anode, 7_Segment10.common_anode, LED4.anode, LED5.anode, J3.pin3
  N47: Part1.A4/SDA, Part2.connector27
  N48: Part1.A5/SCL, Part2.connector26
  N49: Part1.D3_PWM, Part2.connector38
  N50: 14_Segment1.connector0, 14_Segment2.connector0, Part2.connector21, J2.pin2
  N51: 14_Segment1.connector1, 14_Segment2.connector1, Part2.connector42
  N52: 14_Segment1.connector3, 14_Segment2.connector3, Part2.connector41
  N53: 14_Segment1.connector4, 14_Segment2.connector4, Part2.connector40
  N54: 14_Segment1.connector5, 14_Segment2.connector5, Part2.connector18, J2.pin5
  N55: 14_Segment1.connector6, 14_Segment2.connector6, Part2.connector22, J2.pin1
  N56: 14_Segment1.connector8, 14_Segment2.connector8, Part2.connector23
  N57: 14_Segment1.connector9, 14_Segment2.connector9, Part2.connector24
  N58: 14_Segment1.connector10, Part2.connector33, J1.pin3
  N59: 14_Segment1.connector11, 14_Segment2.connector11, Part2.connector25
  N60: 14_Segment1.connector12, 14_Segment2.connector12, Part2.connector19, J2.pin4
  N61: 14_Segment1.connector13, 14_Segment2.connector13, Part2.connector15
  N62: 14_Segment1.connector14, 14_Segment2.connector14, Part2.connector16
  N63: 14_Segment1.connector15, Part2.connector32, J1.pin2
  N64: 14_Segment1.connector16, 14_Segment2.connector16, Part2.connector17
  N65: 14_Segment1.connector17, 14_Segment2.connector17, Part2.connector20, J2.pin3
  N66: 14_Segment2.connector10, Part2.connector31, J1.pin1
  N67: 14_Segment2.connector15, Part2.connector30
